// Logisim project 4bitcpu.circ as structural Verilog: 4 circuits, main circuit fourbitadder
module fourbitadder (
  input  Carry_In,
  input  B4,
  input  B3,
  input  B2,
  input  B1,
  input  A4,
  input  A3,
  input  A2,
  input  A1,
  output Overflow,
  output O4,
  output O3,
  output O2,
  output O1
);

  wire and_1_out, and_2_out, and_3_out, and_4_out, and_5_out, and_6_out, and_7_out, and_8_out, or_2_out,
       or_3_out, or_4_out, xor_1_out, xor_2_out, xor_3_out, xor_4_out;

  and and_1 (and_1_out, B4, A4);
  xor xor_1 (xor_1_out, A4, B4);
  and and_2 (and_2_out, B3, A3);
  xor xor_2 (xor_2_out, A3, B3);
  and and_3 (and_3_out, B2, A2);
  xor xor_3 (xor_3_out, A2, B2);
  and and_4 (and_4_out, B1, A1);
  xor xor_4 (xor_4_out, A1, B1);
  and and_5 (and_5_out, or_2_out, xor_1_out);
  xor xor_5 (O4, xor_1_out, or_2_out);
  and and_6 (and_6_out, or_3_out, xor_2_out);
  xor xor_6 (O3, xor_2_out, or_3_out);
  and and_7 (and_7_out, or_4_out, xor_3_out);
  xor xor_7 (O2, xor_3_out, or_4_out);
  and and_8 (and_8_out, Carry_In, xor_4_out);
  xor xor_8 (O1, xor_4_out, Carry_In);
  or or_1 (Overflow, and_5_out, and_1_out);
  or or_2 (or_2_out, and_6_out, and_2_out);
  or or_3 (or_3_out, and_7_out, and_3_out);
  or or_4 (or_4_out, and_8_out, and_4_out);
endmodule

module cpu (
  input  in_1,
  input  in_2,
  input  in_3,
  input  in_4,
  input  in_5,
  input  LDA,
  input  Clock_Pulse,
  input  Put_Reg_B_On_Bus,
  input  LDB
);

  wire fourbitadder_1_o1, fourbitadder_1_o2, fourbitadder_1_o3, fourbitadder_1_o4, fourbitadder_1_overflow,
       fourbitmux_1_o2, fourbitmux_1_o3, fourbitmux_1_o4, not_1_out, RegisterA_stored_1, RegisterA_stored_2,
       RegisterA_stored_3, RegisterA_stored_4, RegisterB_stored_1, RegisterB_stored_2, RegisterB_stored_3,
       RegisterB_stored_4;

  not not_1 (not_1_out, Put_Reg_B_On_Bus);
  fourbitreg RegisterA (
    .DATA1(in_2), .DATA2(in_3), .DATA3(in_4), .DATA4(in_5), .S(LDA), .C(Clock_Pulse),
    .Stored_1(RegisterA_stored_1), .Stored_2(RegisterA_stored_2), .Stored_3(RegisterA_stored_3),
    .Stored_4(RegisterA_stored_4));
  fourbitmux fourbitmux_1 (
    .A1(RegisterA_stored_1), .A2(RegisterA_stored_2), .A3(RegisterA_stored_3), .A4(RegisterA_stored_4),
    .B1(in_2), .B2(in_3), .B3(in_4), .B4(in_5), .Switch(not_1_out), .O2(fourbitmux_1_o2),
    .O3(fourbitmux_1_o3), .O4(fourbitmux_1_o4));  // open: O1
  fourbitreg RegisterB (
    .DATA1(in_2), .DATA2(in_3), .DATA3(in_4), .DATA4(in_5), .S(LDB), .C(Clock_Pulse),
    .Stored_1(RegisterB_stored_1), .Stored_2(RegisterB_stored_2), .Stored_3(RegisterB_stored_3),
    .Stored_4(RegisterB_stored_4));
  fourbitadder fourbitadder_1 (
    .B4(RegisterB_stored_4), .B3(RegisterB_stored_3), .B2(RegisterB_stored_2), .B1(RegisterB_stored_1),
    .A4(RegisterA_stored_4), .A3(RegisterA_stored_3), .A2(RegisterA_stored_2), .A1(RegisterA_stored_1),
    .Overflow(fourbitadder_1_overflow), .O4(fourbitadder_1_o4), .O3(fourbitadder_1_o3),
    .O2(fourbitadder_1_o2), .O1(fourbitadder_1_o1));  // open: Carry_In
endmodule

module fourbitreg (
  input  DATA1,
  input  DATA2,
  input  DATA3,
  input  DATA4,
  input  S,
  input  C,
  output Stored_1,
  output Stored_2,
  output Stored_3,
  output Stored_4
);

  wire and_1_out, and_2_out, and_3_out, and_4_out, and_5_out, and_6_out, and_7_out, and_8_out, and_9_out,
       and_10_out, and_11_out, and_12_out, nor_1_out, nor_3_out, nor_5_out, nor_7_out, not_1_out, not_2_out,
       not_3_out, not_4_out;

  and and_1 (and_1_out, S, C);
  and and_2 (and_2_out, S, C);
  and and_3 (and_3_out, S, C);
  not not_1 (not_1_out, DATA4);
  and and_4 (and_4_out, S, C);
  and and_5 (and_5_out, DATA1, and_1_out);
  not not_2 (not_2_out, DATA1);
  and and_6 (and_6_out, not_2_out, and_1_out);
  and and_7 (and_7_out, DATA2, and_2_out);
  not not_3 (not_3_out, DATA2);
  and and_8 (and_8_out, not_3_out, and_2_out);
  and and_9 (and_9_out, DATA3, and_3_out);
  not not_4 (not_4_out, DATA3);
  and and_10 (and_10_out, not_4_out, and_3_out);
  and and_11 (and_11_out, DATA4, and_4_out);
  and and_12 (and_12_out, not_1_out, and_4_out);
  nor nor_1 (nor_1_out, and_5_out, Stored_1);
  nor nor_2 (Stored_1, nor_1_out, and_6_out);
  nor nor_3 (nor_3_out, and_7_out, Stored_2);
  nor nor_4 (Stored_2, nor_3_out, and_8_out);
  nor nor_5 (nor_5_out, and_9_out, Stored_3);
  nor nor_6 (Stored_3, nor_5_out, and_10_out);
  nor nor_7 (nor_7_out, and_11_out, Stored_4);
  nor nor_8 (Stored_4, nor_7_out, and_12_out);
endmodule

module fourbitmux (
  input  A1,
  input  A2,
  input  A3,
  input  A4,
  input  B1,
  input  B2,
  input  B3,
  input  B4,
  input  Switch,
  output O1,
  output O2,
  output O3,
  output O4
);

  wire and_1_out, and_2_out, and_3_out, and_4_out, and_5_out, and_6_out, and_7_out, and_8_out, not_1_out,
       not_2_out, not_3_out, not_4_out, not_5_out;

  not not_1 (not_1_out, Switch);
  not not_2 (not_2_out, not_1_out);
  not not_3 (not_3_out, not_1_out);
  not not_4 (not_4_out, not_1_out);
  not not_5 (not_5_out, not_1_out);
  and and_1 (and_1_out, A1, not_1_out);
  and and_2 (and_2_out, B1, not_2_out);
  and and_3 (and_3_out, A2, not_1_out);
  and and_4 (and_4_out, B2, not_3_out);
  and and_5 (and_5_out, A3, not_1_out);
  and and_6 (and_6_out, B3, not_4_out);
  and and_7 (and_7_out, A4, not_1_out);
  and and_8 (and_8_out, B4, not_5_out);
  or or_1 (O1, and_1_out, and_2_out);
  or or_2 (O2, and_3_out, and_4_out);
  or or_3 (O3, and_5_out, and_6_out);
  or or_4 (O4, and_7_out, and_8_out);
endmodule
